// Digital circuit mips_alu.dig as structural Verilog
module mips_alu (
  input  [1:0] alu__op,
  input  [5:0] instr__5__0,
  input  [31:0] A,
  input  [31:0] B,
  output zero,
  output [31:0] result
);

  wire [3:0] u_alu_control_alu_control;

  alu_control #(.applicationType("IVERILOG"), .iverilogOptions("-y .\\"), .CodeFile("C:\\Users\\allan\\source\\repos\\Lab02-ALU\\alu_control.v")) u_alu_control (
    .alu_op(alu__op), .funct(instr__5__0), .alu_control(u_alu_control_alu_control));
  alu #(.applicationType("IVERILOG"), .iverilogOptions("-I C:\\Users\\allan\\source\\repos\\Lab02-ALU\\"), .CodeFile("C:\\Users\\allan\\source\\repos\\Lab02-ALU\\alu.v")) u_alu (
    .alu_control(u_alu_control_alu_control), .A(A), .B(B), .zero(zero), .result(result));
endmodule

/* Test case Test Bench:
alu\_op instr\_5\_0 A          B          zero result
2       0x24        0x1111     0xffff     0    0x1111
2       0x24        0x0000     0xffff     1    0x0000
2       0x25        0x1111     0xffff     0    0xffff
2       0x25        0x0000     0x0000     1    0x0000
2       0x20        0x0001     0xffff     0    0x10000
2       0x20        0x1111     0xffff     0    0x11110
2       0x20        0x0001     0xffffffff 1    0x0000
2       0x20        0x0001     0xfffffffE 0    0xffffffff
2       0x22        0x0001     0xffffffff 0    0x0002
2       0x22        0xffffffff 0x0001     0    0xfffffffe
2       0x22        0xffffffff 0xffffffff 1    0x0000
2       0x22        0x0001     0x0001     1    0x0000
2       0x2A        0x0002     0x0002     1    0x0000
2       0x2A        0x0002     0x0001     1    0x0000
2       0x2A        0x0001     0x0002     0    0x0001
2       0x2A        0xFFFFFFFF 0x0001     0    0x0001
2       0x2A        0x0001     0xFFFFFFFF 1    0x0000
2       0x27        0x1111     0xffff     0    0xffff0000
2       0x27        0x0000     0x0000     0    0xffffffff
0       0x27        0x0001     0xffff     0    0x10000
1       0x2A        0xffff     0x0001     0    0xfffe
1       0x24        0x0001     0x0001     1    0x0000
*/
